// Digital circuit CPU.dig as structural Verilog
module CPU (
  input  clock,
  output [15:0] r0,
  output [15:0] r1,
  output [15:0] r2,
  output [15:0] r3,
  output [3:0] PC,
  output halt,
  output error
);

  wire add, Advance_out, decoder_1_p1, decoder_1_p2, execute_1_p4, hexdisplay_1_p1, hexdisplay_1_p2,
       hexdisplay_1_p3, hexdisplay_1_p4, hexdisplay_2_p1, hexdisplay_2_p2, hexdisplay_2_p3, hexdisplay_2_p4,
       instdisplay_1_p1, instdisplay_1_p2, instdisplay_1_p3, instdisplay_1_p4, instdisplay_1_p5,
       instdisplay_1_p6, jump, move, not_1_out, or_1_out, pm_1_c, pm_1_ld, pm_1_str, regdisplay_1_p1,
       regdisplay_1_p2, regdisplay_2_p1, regdisplay_2_p2, tworeg;
  wire [1:0] rd, rs;
  wire [2:0] op;
  wire [3:0] hexdisplay_1_d1, hexdisplay_1_d2, hexdisplay_1_d3, hexdisplay_1_d4, hexdisplay_2_d1,
       hexdisplay_2_d2, hexdisplay_2_d3, hexdisplay_2_d4, pm_1_a;
  wire [15:0] fecthc_counter_1_instr_0, instdisplay_1_d1, instdisplay_1_d2, instdisplay_1_d3,
       instdisplay_1_d4, instdisplay_1_d5, instdisplay_1_d6, pm_1_d_in, PROGRAM_d, R, regdisplay_1_d1,
       regdisplay_1_d2, regdisplay_2_d1, regdisplay_2_d2;
  wire [31:0] L;

  PM pm_1 (.pc(PC), .A(pm_1_a), .D_in(pm_1_d_in), .str(pm_1_str), .C(pm_1_c), .ld(pm_1_ld));
  SixteenSeg sixteenseg_1 (.led(regdisplay_1_d1), .dp(regdisplay_1_p1));
  SixteenSeg sixteenseg_2 (.led(regdisplay_1_d2), .dp(regdisplay_1_p2));
  REGDISPLAY regdisplay_1 (
    .D1(regdisplay_1_d1), .P1(regdisplay_1_p1), .D2(regdisplay_1_d2), .P2(regdisplay_1_p2), .E(1'b1),
    .J(jump), .R(rd));
  EEPROMDualPort #(.AddrBits(4), .isProgramMemory("true"), .Bits(16)) PROGRAM (
    .A(pm_1_a), .Din(pm_1_d_in), .str(pm_1_str), .C(pm_1_c), .ld(pm_1_ld), .D(PROGRAM_d));
  not not_1 (not_1_out, jump);
  fecthc_counter fecthc_counter_1 (
    .instr_i(PROGRAM_d), .clock(or_1_out), .value(R), .jump(jump), .instr_0(fecthc_counter_1_instr_0), .PC(PC));
  Button Advance (.out(Advance_out));
  Seven_Seg_Hex seven_seg_hex_1 (.d(hexdisplay_1_d1), .dp(hexdisplay_1_p1));
  Seven_Seg_Hex seven_seg_hex_2 (.d(hexdisplay_1_d2), .dp(hexdisplay_1_p2));
  hexdisplay hexdisplay_1 (
    .D1(hexdisplay_1_d1), .P1(hexdisplay_1_p1), .D2(hexdisplay_1_d2), .P2(hexdisplay_1_p2),
    .D3(hexdisplay_1_d3), .P3(hexdisplay_1_p3), .D4(hexdisplay_1_d4), .P4(hexdisplay_1_p4), .E(not_1_out),
    .V(L));  // open: D5, P5, D6, P6, D7, P7, D8, P8
  or or_1 (or_1_out, clock, Advance_out);
  Seven_Seg_Hex seven_seg_hex_3 (.d(hexdisplay_1_d3), .dp(hexdisplay_1_p3));
  Seven_Seg_Hex seven_seg_hex_4 (.d(hexdisplay_1_d4), .dp(hexdisplay_1_p4));
  // decoder decoder_1: pin names not known; wires that end beside it: decoder_1_p1, decoder_1_p2, fecthc_counter_1_instr_0, rs, rd, L, R, op, add, jump, move, tworeg
  SixteenSeg sixteenseg_3 (.led(instdisplay_1_d1), .dp(instdisplay_1_p1));
  SixteenSeg sixteenseg_4 (.led(instdisplay_1_d2), .dp(instdisplay_1_p2));
  SixteenSeg sixteenseg_5 (.led(instdisplay_1_d3), .dp(instdisplay_1_p3));
  instdisplay instdisplay_1 (
    .D1(instdisplay_1_d1), .P1(instdisplay_1_p1), .D2(instdisplay_1_d2), .P2(instdisplay_1_p2),
    .D3(instdisplay_1_d3), .P3(instdisplay_1_p3), .D4(instdisplay_1_d4), .P4(instdisplay_1_p4),
    .D5(instdisplay_1_d5), .P5(instdisplay_1_p5), .D6(instdisplay_1_d6), .P6(instdisplay_1_p6), .i(op));
  SixteenSeg sixteenseg_6 (.led(instdisplay_1_d4), .dp(instdisplay_1_p4));
  SixteenSeg sixteenseg_7 (.led(instdisplay_1_d5), .dp(instdisplay_1_p5));
  SixteenSeg sixteenseg_8 (.led(instdisplay_1_d6), .dp(instdisplay_1_p6));
  Seven_Seg_Hex seven_seg_hex_5 (.d(hexdisplay_2_d1), .dp(hexdisplay_2_p1));
  Seven_Seg_Hex seven_seg_hex_6 (.d(hexdisplay_2_d2), .dp(hexdisplay_2_p2));
  Seven_Seg_Hex seven_seg_hex_7 (.d(hexdisplay_2_d3), .dp(hexdisplay_2_p3));
  hexdisplay hexdisplay_2 (
    .D1(hexdisplay_2_d1), .P1(hexdisplay_2_p1), .D2(hexdisplay_2_d2), .P2(hexdisplay_2_p2),
    .D3(hexdisplay_2_d3), .P3(hexdisplay_2_p3), .D4(hexdisplay_2_d4), .P4(hexdisplay_2_p4), .E(1'b1), .V(R));
  // execute execute_1: pin names not known; wires that end beside it: L, R, op, execute_1_p4, halt, error
  Seven_Seg_Hex seven_seg_hex_8 (.d(hexdisplay_2_d4), .dp(hexdisplay_2_p4));
  SixteenSeg sixteenseg_9 (.led(regdisplay_2_d1), .dp(regdisplay_2_p1));
  REGDISPLAY regdisplay_2 (
    .D1(regdisplay_2_d1), .P1(regdisplay_2_p1), .D2(regdisplay_2_d2), .P2(regdisplay_2_p2), .E(tworeg),
    .J(1'b0), .R(rs));
  SixteenSeg sixteenseg_10 (.led(regdisplay_2_d2), .dp(regdisplay_2_p2));
  // reg_file reg_file_1: pin names not known; wires that end beside it: rs, rd, execute_1_p4, or_1_out, decoder_1_p1, decoder_1_p2, r0, r1, r2, r3

  // Notes on the sheet:
  //   contents of PROGRAM (hex, n*v repeats v):
  //   120,61,bd,91,7d,10e
  //   L / DST
  //   R / SRC / VAL
endmodule
