// Digital circuit decoder.dig as structural Verilog
module decoder (
  input  [31:0] instruction,
  output [15:0] A,
  output [15:0] B
);


  assign A = instruction[15:0];
  assign B = instruction[31:16];
endmodule
