// Digital circuit execute.dig as structural Verilog
module execute (
  input  [15:0] value,
  input  [15:0] B,
  input  add,
  output [15:0] result
);

  wire [15:0] Add_s;

  Add #(.Bits(16)) u_Add (.a(value), .b(B), .c_i(1'b0), .s(Add_s));  // open: c_o
  Multiplexer #(.Bits(16)) multiplexer_1 (.sel(add), .in_0(B), .in_1(Add_s), .out(result));

  // Notes on the sheet:
  //   value: default 1
  //   B: default 2
endmodule
